# Fritzing sketch NodeMCU (saved by Fritzing 0.9.3b)
breadboards: 1

parts:
  U1 = NodeMCU V1.0
  LED1 = LED - 5mm [color="Green (560nm)" package="5 mm [THT]"]
  LED2 = LED - 5mm [color="Red (633nm)" package="5 mm [THT]"]
  S1 = Pushbutton [package="[THT]"]

nets:
  N1: U1.D1, U1.GND, LED1.cathode, LED2.cathode, S1.Pin_3, S1.Pin_4
  N2: U1.D2, LED1.anode
  N3: U1.D3, S1.Pin_1, S1.Pin_2

custom parts:
  NodeMCU V1.0: ESP8266 based NodeMCU
